# Fritzing sketch smartRoomControllerFritzing (saved by Fritzing 0.9.9b)
breadboards: 1

parts:
  Teensy_3_1 = Teensy 3.1
  S1 = Pushbutton [package="[THT]"]
  R1 = Resistor [tolerance=±5% power=0.25 resistance=220 package=THT]
  Part1 = 12 NeoPixel Ring [part_number=1643]
  OLED_I2C1 = OLED 128x64 I2C Monochrome Display
  Part2 = Passive Buzzer
  PIR1 = PIR sensor
  WIZ820io1 = WIZ820io [part_number=WIZ820io]

nets:
  GND: Teensy_3_1.GND, R1.Pin_1, Part1.GND, OLED_I2C1.GND, Part2.GND, PIR1.GND, WIZ820io1.GND
  N1: Teensy_3_1.D1, PIR1.SIG
  N2: Teensy_3_1.D2, Part2.NC
  N3: Teensy_3_1.D5, Part1.IN
  N4: Teensy_3_1.D9, WIZ820io1.nRESET
  N5: Teensy_3_1.D10, WIZ820io1.nSS
  N6: Teensy_3_1.D11, WIZ820io1.MOSI
  N7: Teensy_3_1.D12, WIZ820io1.MISO
  N8: Teensy_3_1.D13, WIZ820io1.SCLK
  N9: Teensy_3_1.A4/D18, OLED_I2C1.SDA
  N10: Teensy_3_1.A5/D19, OLED_I2C1.SCK
  N11: Teensy_3_1.A9/D23, S1.Pin_1, S1.Pin_2, R1.Pin_0
  VDD: Teensy_3_1.3V3, S1.Pin_3, S1.Pin_4, Part1.VDD, OLED_I2C1.VDD, Part2.S, PIR1.VDD, WIZ820io1.VIN

custom parts:
  Pushbutton: A generic pushbutton.
  12 NeoPixel Ring: 12 ultra bright smart LED NeoPixels are arranged in a circle with 1.5" (37mm) outer diameter. The rings are 'chainable' - connect the output pin of one to the input pin of another. Use only one microcontroller pin to control as many as you can chain together! Each LED is addressable as the driver chip is inside the LED. Each one has ~18mA constant current drive so the color will be very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
